// Logisim project 16 Bit Control Unit.circ as structural Verilog: 1 circuit, main circuit Control Unit
module Control_Unit (
  input  [3:0] Opcode,
  output RegDst,
  output RegWrite,
  output ALUSrc,
  output MemWrite,
  output MemRead,
  output MemToReg,
  output PCSrc,
  output [1:0] ALUOp
);

  wire ADDI_out, LUI_out;

  and R (ALUOp[1], Opcode[3], ~Opcode[2], Opcode[1], ~Opcode[0]);  // AND_Gate
  and LW (MemRead, ~Opcode[3], ~Opcode[2], ~Opcode[1], ~Opcode[0]);  // AND_Gate
  and SW (MemWrite, ~Opcode[3], ~Opcode[2], ~Opcode[1], Opcode[0]);  // AND_Gate
  and BEQ (ALUOp[0], ~Opcode[3], ~Opcode[2], Opcode[1], ~Opcode[0]);  // AND_Gate
  and ADDI (ADDI_out, ~Opcode[3], ~Opcode[2], Opcode[1], Opcode[0]);  // AND_Gate
  and LUI (LUI_out, ~Opcode[3], Opcode[2], ~Opcode[1], ~Opcode[0]);  // AND_Gate
  or or_1 (RegWrite, MemRead, LUI_out, ADDI_out, ALUOp[1]);
  or or_2 (ALUSrc, MemRead, LUI_out, ADDI_out, MemWrite);

  assign MemToReg = MemRead;
  assign PCSrc = ALUOp[0];
  assign RegDst = ALUOp[1];

  // Notes on the sheet:
  //   NOTE:
  //   R >> 1010
  //   LW >> 0000
  //   SW >> 0001
  //   BEQ >> 0010
  //   ADDI >> 0011
  //   LUI >> 0100
endmodule
