// Logisim project Datapath.circ as structural Verilog: 2 circuits, main circuit Datapath
module Datapath (
  input  Clr,
  input  Reset,
  output [3:0] OpCode,
  output [15:0] PC_Final,
  output [15:0] PC,
  output [15:0] PC_2,
  output [2:0] rs,
  output [2:0] rt,
  output [2:0] rd,
  output [15:0] out_10,
  output Zero,
  output [2:0] out_12,
  output Cout,
  output [15:0] After,
  output [5:0] Before
);

  wire ALS, BEQ_out, Cin, Clk, MR, MTR, MW, PC_t, RD_t, RW;
  wire [1:0] alu_control_1_operation, ALUOp;
  wire [15:0] adder_2_out, multiplexer_2_out, n16_bit_alu_1_result, n16_bit_register_1_out_8,
       n16_bit_register_1_out_9, ram_1_data;

  Register #(.width(16)) u_PC (.D(PC_Final), .Q(PC), .clk(Clk), .clr(Reset));  // open: en
  Clock Clock (.out(Clk));
  Adder #(.width(16)) adder_1 (.a(PC), .b(16'h1), .out(PC_2));  // open: cin, cout
  ROM #(.addrWidth(16), .dataWidth(16)) rom_1 (.addr(PC), .data({OpCode, rs, rt, Before}));  // open: sel
  Multiplexer #(.width(3), .enable("false")) multiplexer_1 (.in0(rt), .in1(Before[5:3]), .out(rd), .sel(RD_t));
  Control_Unit control_unit_1 (
    .Opcode(OpCode), .RegDst(RD_t), .RegWrite(RW), .ALUSrc(ALS), .MemWrite(MW), .MemRead(MR), .MemToReg(MTR),
    .PCSrc(PC_t), .ALUOp(ALUOp));
  assign After = {{10{Before[5]}}, Before};  // Bit_Extender bit_extender_1
  _16_Bit_Register u_16_bit_register_1 (
    .out_8(n16_bit_register_1_out_8), .out_9(n16_bit_register_1_out_9), .Clock(Clk), .Write_Data(out_10),
    .Register_Selector(rd), .Rs(rs), .Rt(rt), .RegWrite(RW), .Clear(Clr));
  Multiplexer #(.width(16), .enable("false")) multiplexer_2 (
    .in0(n16_bit_register_1_out_9), .in1(After), .out(multiplexer_2_out), .sel(ALS));
  ALU_Control alu_control_1 (.Function(Before[2:0]), .ALUOp(ALUOp), .Operation({Cin, alu_control_1_operation}));
  _16_bit_ALU u_16_bit_alu_1 (
    .A(n16_bit_register_1_out_8), .B(multiplexer_2_out), .Result(n16_bit_alu_1_result), .Zero(Zero),
    .Cout(Cout), .Sub(Cin), .Cin(Cin), .Operation(alu_control_1_operation));
  Multiplexer #(.width(16), .enable("false")) multiplexer_3 (
    .in0(PC_2), .in1(adder_2_out), .out(PC_Final), .sel(BEQ_out));
  Adder #(.width(16)) adder_2 (.a(PC_2), .b(After), .out(adder_2_out));  // open: cin, cout
  and BEQ (BEQ_out, Zero, PC_t);
  RAM #(.addrWidth(16), .dataWidth(16), .bus("separate")) ram_1 (
    .addr(n16_bit_alu_1_result), .din(n16_bit_register_1_out_9), .data(ram_1_data), .str(MW), .clk(Clk),
    .ld(MR));  // open: sel, clr
  Multiplexer #(.width(16), .enable("false")) multiplexer_4 (
    .in0(n16_bit_alu_1_result), .in1(ram_1_data), .out(out_10), .sel(MTR));

  assign out_12 = Before[2:0];

  // Other names for the same wires on the sheet: Fun[2:0] = Before[2:0]

  // Notes on the sheet:
  //   ROM
  //   PC+2
  //   contents of rom_1 (hex, n*v repeats v):
  //   31c0 a010 30ca a4cb 2045 b00 a9f8 3481 3b41 2039 11fb
  //   RAM
endmodule

module ALU_Control (
  input  [2:0] Function,
  input  [1:0] ALUOp,
  output [2:0] Operation
);

  wire and_1_out;

  and and_1 (and_1_out, Function[1], ALUOp[1]);
  or or_1 (Operation[1], ~ALUOp[1], ~Function[2]);  // OR_Gate
  and and_2 (Operation[0], Function[0], ALUOp[1]);
  or or_2 (Operation[2], ALUOp[0], and_1_out);

  // Notes on the sheet:
  //   BEQ
endmodule
